// Logisim project somaN.circ as structural Verilog: 1 circuit, main circuit main
module main (
  input  [7:0] N,
  output [15:0] out_2
);

  wire and_1_out, button_1_out, clock_1_out, comparator_1_eq;
  wire [7:0] adder_1_out, counter_1_q;
  wire [15:0] adder_2_out;

  Button button_1 (.out(button_1_out));
  Clock clock_1 (.out(clock_1_out));
  and and_1 (and_1_out, clock_1_out, ~comparator_1_eq);  // AND_Gate
  Counter counter_1 (.Q(counter_1_q), .clk(and_1_out), .clr(button_1_out));  // open: load, D, count, carry
  Adder adder_1 (.a(N), .b(8'h1), .out(adder_1_out));  // open: cin, cout
  Adder #(.width(16)) adder_2 (.a({{8{1'b0}}, counter_1_q}), .b(out_2), .out(adder_2_out));  // open: cin, cout
  Comparator comparator_1 (.a(adder_1_out), .b(counter_1_q), .eq(comparator_1_eq));  // open: gt, lt
  Register #(.width(16)) register_1 (.D(adder_2_out), .Q(out_2), .clk(and_1_out), .clr(button_1_out));  // open: en
endmodule
